# Fritzing sketch HC595ESP32V001 (saved by Fritzing 1.0.3b)
circuit board: 4.47407cm x 12.3942cm
breadboards: 1

parts:
  ULN2803APG = Darlington Driver [package=dil18]
  74HC595N = SHIFT REGISTER [package=dil16]
  74HC595N_2 = SHIFT REGISTER [package=dil16]
  74HC595N_3 = SHIFT REGISTER [package=dil16]
  ULN2803APG_2 = Darlington Driver [package=dil18]
  ULN2803APG_3 = Darlington Driver [package=dil18]
  C2 = Electrolytic Capacitor [capacitance=10µF voltage=25V package="100 mil [THT, electrolytic]"]
  D2 = Rectifier Diode [part_number=1N5817 package="300 mil [THT]"]
  Q2 = PNP-Transistor [part_number=BC547 package="TO92 [THT]"]
  Q3 = PNP-Transistor [part_number=BC327 package="TO92 [THT]"]
  R7 = Resistor [tolerance=±5% resistance=10k power=0.25 package=THT]
  R8 = Resistor [tolerance=±5% resistance=4.7k power=0.25 package=THT]
  J6 = screw terminal, 2 pins
  74HC595N1 = SHIFT REGISTER [package=dil16]
  ULN2803APG1 = Darlington Driver [package=dil18]
  R10 = Resistor [tolerance=±5% resistance=10k power=0.25 package=THT]
  R9 = Resistor [tolerance=±5% power=0.25 resistance=10k package=THT]
  ESP32_connect = female pin header, 6 pins [form="♀ (female)"]

nets:
  N1: ULN2803APG.1, 74HC595N.QH
  N2: ULN2803APG.2, 74HC595N.QG
  N3: ULN2803APG.3, 74HC595N.QF
  N4: ULN2803APG.4, 74HC595N.QE
  N5: ULN2803APG.5, 74HC595N.QD
  N6: ULN2803APG.6, 74HC595N.QC
  N7: ULN2803APG.7, 74HC595N.QB
  N8: ULN2803APG.8, 74HC595N.QA
  GND: ULN2803APG.9, 74HC595N.GND, 74HC595N.G, 74HC595N_2.GND, 74HC595N_2.G, 74HC595N_3.GND, 74HC595N_3.G, ULN2803APG_2.9, ULN2803APG_3.9, C2.-, J6.pin1, 74HC595N1.GND, 74HC595N1.G, ULN2803APG1.9, R10.Pin_1, ESP32_connect.pin5
  N9: ULN2803APG.10, ULN2803APG_2.10, ULN2803APG_3.10, D2.cathode, ULN2803APG1.10
  N10: 74HC595N.QH*, 74HC595N1.SER
  VCC: 74HC595N.SCL, 74HC595N.VCC, 74HC595N_2.SCL, 74HC595N_2.VCC, 74HC595N_3.SCL, 74HC595N_3.VCC, 74HC595N1.SCL, 74HC595N1.VCC, ESP32_connect.pin6
  N11: 74HC595N.SCK, 74HC595N_2.SCK, 74HC595N_3.SCK, 74HC595N1.SCK, ESP32_connect.pin2
  N12: 74HC595N.RCK, 74HC595N_2.RCK, 74HC595N_3.RCK, 74HC595N1.RCK, ESP32_connect.pin3
  N13: 74HC595N.SER, 74HC595N_2.QH*
  N14: 74HC595N_2.QB, ULN2803APG_2.7
  N15: 74HC595N_2.QC, ULN2803APG_2.6
  N16: 74HC595N_2.QD, ULN2803APG_2.5
  N17: 74HC595N_2.QE, ULN2803APG_2.4
  N18: 74HC595N_2.QF, ULN2803APG_2.3
  N19: 74HC595N_2.QG, ULN2803APG_2.2
  N20: 74HC595N_2.QH, ULN2803APG_2.1
  N21: 74HC595N_2.SER, 74HC595N_3.QH*
  N22: 74HC595N_2.QA, ULN2803APG_2.8
  N23: 74HC595N_3.QB, ULN2803APG_3.7
  N24: 74HC595N_3.QC, ULN2803APG_3.6
  N25: 74HC595N_3.QD, ULN2803APG_3.5
  N26: 74HC595N_3.QE, ULN2803APG_3.4
  N27: 74HC595N_3.QF, ULN2803APG_3.3
  N28: 74HC595N_3.QG, ULN2803APG_3.2
  N29: 74HC595N_3.QH, ULN2803APG_3.1
  N30: 74HC595N_3.SER, ESP32_connect.pin4
  N31: 74HC595N_3.QA, ULN2803APG_3.8
  N32: C2.+, Q3.E, J6.pin2
  N33: D2.anode, Q3.C, R7.Pin_0
  N34: Q2.E, R7.Pin_1
  N35: Q2.B, R9.Pin_0
  N36: Q2.C, R8.Pin_1
  N37: Q3.B, R8.Pin_0
  N38: 74HC595N1.QB, ULN2803APG1.7
  N39: 74HC595N1.QC, ULN2803APG1.6
  N40: 74HC595N1.QD, ULN2803APG1.5
  N41: 74HC595N1.QE, ULN2803APG1.4
  N42: 74HC595N1.QF, ULN2803APG1.3
  N43: 74HC595N1.QG, ULN2803APG1.2
  N44: 74HC595N1.QH, ULN2803APG1.1
  N45: 74HC595N1.QA, ULN2803APG1.8
  N46: R10.Pin_0, R9.Pin_1, ESP32_connect.pin1

notes:
  12V
  Gnd
  +  1  2  3  4  5  6  7  8
  + 17 18 19 20 21 22 23 24
  +  9 10 11 12 13 14 15 16
  +
  -
  PWM
  + 25 26 27 28 29 30 31 32
  3V3
  A0 D17
  A1 D18
  A2 D19
  A7 D24
  V01 ESP32 HC595 Ed Nieuwenhuys 2024

// code stored in the sketch: Untitled2.ino
// V002 -> V003 Changed D13 to D10
